// Logisim project TallerLogica-Secuenciales.circ as structural Verilog: 6 circuits, main circuit buffer_tres_estados
module buffer_tres_estados (
  input  A,
  input  A_en,
  input  B,
  input  B_en,
  input  C,
  input  C_en,
  output Res
);

  assign Res = A_en ? A : 1'bz;  // Controlled_Buffer controlled_buffer_1
  assign Res = B_en ? B : 1'bz;  // Controlled_Buffer controlled_buffer_2
  assign Res = C_en ? C : 1'bz;  // Controlled_Buffer controlled_buffer_3
endmodule

module registro_salida_restringida (
  input  en_out,
  input  Reg_in,
  input  clk,
  input  w,
  output Reg_Debug,
  output Reg_output
);

  wire and_1_out;

  and and_1 (and_1_out, clk, w);
  D_Flip_Flop d_ff_1 (.D(Reg_in), .clk(and_1_out), .Q(Reg_Debug));  // open: Qn, preset, reset
  assign Reg_output = en_out ? Reg_Debug : 1'bz;  // Controlled_Buffer controlled_buffer_1
endmodule

module registro_4bytes_salida (
  input  [3:0] Reg4_in,
  input  en_out,
  input  clk,
  input  w,
  output [3:0] Reg4_Debug,
  output [3:0] Reg4_output
);

  registro_salida_restringida registro_salida_restringida_1 (
    .en_out(en_out), .Reg_in(Reg4_in[0]), .clk(clk), .w(w), .Reg_Debug(Reg4_Debug[0]),
    .Reg_output(Reg4_output[0]));
  registro_salida_restringida registro_salida_restringida_2 (
    .en_out(en_out), .Reg_in(Reg4_in[1]), .clk(clk), .w(w), .Reg_Debug(Reg4_Debug[1]),
    .Reg_output(Reg4_output[1]));
  registro_salida_restringida registro_salida_restringida_3 (
    .en_out(en_out), .Reg_in(Reg4_in[2]), .clk(clk), .w(w), .Reg_Debug(Reg4_Debug[2]),
    .Reg_output(Reg4_output[2]));
  registro_salida_restringida registro_salida_restringida_4 (
    .en_out(en_out), .Reg_in(Reg4_in[3]), .clk(clk), .w(w), .Reg_Debug(Reg4_Debug[3]),
    .Reg_output(Reg4_output[3]));
endmodule

module ALU_regs (
  input  clk,
  input  [3:0] A,
  input  in_3,
  input  A_Write,
  input  [3:0] B,
  input  B_Write,
  input  [1:0] OP,
  output [3:0] A_Debug,
  output [3:0] B_Debug,
  output N,
  output [3:0] S_Debug,
  output [3:0] Reg4_output,
  output Z,
  output V,
  output C
);

  wire alu_1_p5, not_1_out;
  wire [3:0] alu_1_p9, registro_4bytes_salida_1_reg4_output, registro_4bytes_salida_2_reg4_output;

  Hex_Digit_Display hex_digit_display_1 (.value(A_Debug));  // open: dp
  registro_4bytes_salida registro_4bytes_salida_1 (
    .Reg4_in(A), .en_out(1'b1), .clk(clk), .w(A_Write), .Reg4_Debug(A_Debug),
    .Reg4_output(registro_4bytes_salida_1_reg4_output));
  registro_4bytes_salida registro_4bytes_salida_2 (
    .Reg4_in(B), .en_out(1'b1), .clk(clk), .w(B_Write), .Reg4_Debug(B_Debug),
    .Reg4_output(registro_4bytes_salida_2_reg4_output));
  Hex_Digit_Display hex_digit_display_2 (.value(B_Debug));  // open: dp
  Hex_Digit_Display hex_digit_display_3 (.value(alu_1_p9));  // open: dp
  // ALU alu_1: pin names not known; wires that end beside it: registro_4bytes_salida_1_reg4_output, registro_4bytes_salida_2_reg4_output, OP, N, alu_1_p5, V, V, C, alu_1_p9, alu_1_p5, Z
  not not_1 (not_1_out, clk);
  Hex_Digit_Display hex_digit_display_4 (.value(S_Debug));  // open: dp
  registro_4bytes_salida registro_4bytes_salida_3 (
    .Reg4_in(alu_1_p9), .en_out(in_3), .clk(not_1_out), .w(1'b1), .Reg4_Debug(S_Debug),
    .Reg4_output(Reg4_output));
endmodule

module ej_02 (
  input  in_1,
  input  in_2,
  input  in_3,
  input  in_4,
  input  clk,
  input  Force_Input,
  input  in_7,
  input  in_8,
  input  en_Force_Input,
  output R0,
  output out_11,
  output R1,
  output R2
);

  assign out_11 = en_Force_Input ? Force_Input : 1'bz;  // Controlled_Buffer controlled_buffer_1
  registro_salida_restringida registro_salida_restringida_1 (
    .en_out(clk), .Reg_in(out_11), .clk(in_1), .w(in_2), .Reg_Debug(R0), .Reg_output(out_11));
  registro_salida_restringida registro_salida_restringida_2 (
    .en_out(clk), .Reg_in(out_11), .clk(in_3), .w(in_4), .Reg_Debug(R1), .Reg_output(out_11));
  registro_salida_restringida registro_salida_restringida_3 (
    .en_out(clk), .Reg_in(out_11), .clk(in_7), .w(in_8), .Reg_Debug(R2), .Reg_output(out_11));
endmodule

module ej_03 (
  input  clk,
  input  ALU_A_Write,
  input  ALU_B_Write,
  input  [1:0] OP,
  input  ALU_enableOut,
  input  Reg0_enableOut,
  input  Reg0_Write,
  input  Reg1_enableOut,
  input  Reg1_Write,
  input  Reg2_enableOut,
  input  Reg2_Write,
  input  Reg3_enableOut,
  input  Reg3_Write,
  input  [3:0] Force_Input,
  input  en_Force_Input,
  output N,
  output Z,
  output V,
  output C
);

  wire [3:0] alu_regs_1_p8, alu_regs_1_p9, alu_regs_1_p14, controlled_buffer_1_out, Registro_00_reg4_debug,
       Registro_01_reg4_debug, Registro_01_reg4_output, Registro_02_reg4_debug, Registro_03_reg4_debug;

  assign controlled_buffer_1_out = en_Force_Input ? Force_Input : 4'bz;  // Controlled_Buffer controlled_buffer_1
  registro_4bytes_salida Registro_01 (
    .Reg4_in(controlled_buffer_1_out), .en_out(Reg1_enableOut), .clk(clk), .w(Reg1_Write),
    .Reg4_Debug(Registro_01_reg4_debug), .Reg4_output(Registro_01_reg4_output));
  registro_4bytes_salida Registro_02 (
    .Reg4_in(controlled_buffer_1_out), .en_out(Reg2_enableOut), .clk(clk), .w(Reg2_Write),
    .Reg4_Debug(Registro_02_reg4_debug), .Reg4_output(Registro_01_reg4_output));
  registro_4bytes_salida Registro_03 (
    .Reg4_in(controlled_buffer_1_out), .en_out(Reg3_enableOut), .clk(clk), .w(Reg3_Write),
    .Reg4_Debug(Registro_03_reg4_debug), .Reg4_output(Registro_01_reg4_output));
  Hex_Digit_Display hex_digit_display_1 (.value(Registro_00_reg4_debug));  // open: dp
  registro_4bytes_salida Registro_00 (
    .Reg4_in(controlled_buffer_1_out), .en_out(Reg0_enableOut), .clk(clk), .w(Reg0_Write),
    .Reg4_Debug(Registro_00_reg4_debug), .Reg4_output(Registro_01_reg4_output));
  Hex_Digit_Display hex_digit_display_2 (.value(Registro_01_reg4_debug));  // open: dp
  Hex_Digit_Display hex_digit_display_3 (.value(Registro_02_reg4_debug));  // open: dp
  Hex_Digit_Display hex_digit_display_4 (.value(Registro_03_reg4_debug));  // open: dp
  Hex_Digit_Display hex_digit_display_5 (.value(alu_regs_1_p8));  // open: dp
  Hex_Digit_Display Bus_2 (.value(controlled_buffer_1_out));  // open: dp
  Hex_Digit_Display hex_digit_display_6 (.value(alu_regs_1_p9));  // open: dp
  // ALU_regs alu_regs_1: pin names not known; wires that end beside it: clk, Registro_01_reg4_output, ALU_A_Write, Registro_01_reg4_output, ALU_B_Write, ALU_enableOut, OP, alu_regs_1_p8, alu_regs_1_p9, N, Z, V, C, alu_regs_1_p14, controlled_buffer_1_out
  Hex_Digit_Display hex_digit_display_7 (.value(alu_regs_1_p14));  // open: dp
endmodule
