// Logisim project TallerLogica_Combinatorios.circ as structural Verilog: 12 circuits, main circuit sumador_simple
module sumador_simple (
  input  A,
  input  B,
  output S,
  output Cout
);

  xor xor_1 (S, A, B);
  and and_1 (Cout, A, B);
endmodule

module sumador_completo (
  input  Cin,
  input  A,
  input  B,
  output S,
  output Cout
);

  wire sumador_simple_1_cout, sumador_simple_1_s, sumador_simple_2_cout;

  sumador_simple sumador_simple_1 (.A(A), .B(B), .S(sumador_simple_1_s), .Cout(sumador_simple_1_cout));
  sumador_simple sumador_simple_2 (.A(Cin), .B(sumador_simple_1_s), .S(S), .Cout(sumador_simple_2_cout));
  or or_1 (Cout, sumador_simple_2_cout, sumador_simple_1_cout);
endmodule

module sumador_4 (
  input  Cin,
  input  [3:0] A,
  input  [3:0] B,
  output [3:0] S,
  output Cout
);

  wire sumador_completo_1_cout, sumador_completo_2_cout, sumador_completo_3_cout;

  sumador_completo sumador_completo_1 (.Cin(Cin), .A(A[0]), .B(B[0]), .S(S[0]), .Cout(sumador_completo_1_cout));
  sumador_completo sumador_completo_2 (
    .Cin(sumador_completo_1_cout), .A(A[1]), .B(B[1]), .S(S[1]), .Cout(sumador_completo_2_cout));
  sumador_completo sumador_completo_3 (
    .Cin(sumador_completo_2_cout), .A(A[2]), .B(B[2]), .S(S[2]), .Cout(sumador_completo_3_cout));
  sumador_completo sumador_completo_4 (.Cin(sumador_completo_3_cout), .A(A[3]), .B(B[3]), .S(S[3]), .Cout(Cout));
  Hex_Digit_Display hex_digit_display_1 (.value(S));  // open: dp
endmodule

module comparador_cero (
  input  [3:0] A,
  output Z
);

  wire nor_1_out, nor_2_out;

  nor nor_1 (nor_1_out, A[0], A[1]);
  nor nor_2 (nor_2_out, A[2], A[3]);
  and and_1 (Z, nor_1_out, nor_2_out);
endmodule

module sumador_flags (
  input  Cin,
  input  [3:0] A,
  input  [3:0] B,
  output V,
  output N,
  output [3:0] S,
  output Z,
  output C
);

  check_overflow_c2 check_overflow_c2_1 (.MS1(A[3]), .MS2(B[3]), .Res(N), .overflow(V));
  sumador_4 sumador_4_1 (.Cin(Cin), .A(A), .B(B), .S({N, S[2:0]}), .Cout(C));
  Hex_Digit_Display hex_digit_display_1 (.value({N, S[2:0]}));  // open: dp
  comparador_cero comparador_cero_1 (.A({N, S[2:0]}), .Z(Z));

  assign S[3] = N;
endmodule

module incrementador_4 (
  input  [3:0] A,
  output [3:0] S
);

  sumador_4 sumador_4_1 (.Cin(1'b1), .A(A), .B(4'b0000), .S(S));  // open: Cout
  Hex_Digit_Display hex_digit_display_1 (.value(S));  // open: dp
endmodule

module inversor_4 (
  input  [3:0] A,
  input  INV,
  output [3:0] S
);

  wire [3:0] incrementador_4_1_s, not_2_out;

  not not_1 (not_2_out[1], A[1]);
  not not_2 (not_2_out[0], A[0]);
  not not_3 (not_2_out[2], A[2]);
  not not_4 (not_2_out[3], A[3]);
  incrementador_4 incrementador_4_1 (.A(not_2_out), .S(incrementador_4_1_s));
  Multiplexer #(.width(4)) multiplexer_1 (.in0(A), .in1(incrementador_4_1_s), .out(S), .sel(INV));
  Hex_Digit_Display hex_digit_display_1 (.value(S));  // open: dp
endmodule

module ALU (
  input  [3:0] A,
  input  [3:0] B,
  input  [1:0] OP,
  output N,
  output [3:0] S,
  output Z,
  output V,
  output C
);

  wire not_1_out, sumador_flags_1_c, sumador_flags_1_v;
  wire [3:0] and_4bit_a_bit_1_res, inversor_4_1_s, or_4bit_a_bit_1_res, sumador_flags_1_s;

  inversor_4 inversor_4_1 (.A(B), .INV(OP[0]), .S(inversor_4_1_s));
  sumador_flags sumador_flags_1 (
    .Cin(1'b0), .A(A), .B(inversor_4_1_s), .V(sumador_flags_1_v), .S(sumador_flags_1_s), .C(sumador_flags_1_c));  // open: N, Z
  AND_4bit_a_bit and_4bit_a_bit_1 (.A(A), .B(B), .Res(and_4bit_a_bit_1_res));
  OR_4bit_a_bit or_4bit_a_bit_1 (.A(A), .B(B), .Res(or_4bit_a_bit_1_res));
  not not_1 (not_1_out, sumador_flags_1_c);
  Multiplexer #(.select(2), .width(4)) multiplexer_1 (
    .in0(sumador_flags_1_s), .in1(sumador_flags_1_s), .in2(and_4bit_a_bit_1_res), .in3(or_4bit_a_bit_1_res),
    .out({N, S[2:0]}), .sel(OP));
  Multiplexer #(.select(2)) multiplexer_2 (
    .in0(sumador_flags_1_v), .in1(sumador_flags_1_v), .in2(1'b0), .in3(1'b0), .out(V), .sel(OP));
  Multiplexer #(.select(2)) multiplexer_3 (
    .in0(sumador_flags_1_c), .in1(not_1_out), .in2(1'b0), .in3(1'b0), .out(C), .sel(OP));
  Hex_Digit_Display hex_digit_display_1 (.value({N, S[2:0]}));  // open: dp
  comparador_cero comparador_cero_1 (.A({N, S[2:0]}), .Z(Z));

  assign S[3] = N;
endmodule

module verificador (
  output [3:0] out_1,
  output [3:0] out_2,
  output [1:0] out_3,
  output halt,
  output N,
  output Z,
  output V,
  output C,
  output [3:0] res
);

  wire clock_1_out;

  Clock clock_1 (.out(clock_1_out));
  Counter #(.max('h3ff), .width(10)) counter_1 (
    .clk(clock_1_out), .carry(halt), .Q({out_3, out_2, out_1}));  // open: clr, load, up, count, D
  // ALU alu_1: pin names not known; wires that end beside it: out_1, out_2, out_3, N, Z, V, C, res
endmodule

module check_overflow_c2 (
  input  MS1,
  input  MS2,
  input  Res,
  output overflow
);

  wire not_1_out, xor_1_out, xor_2_out;

  xor xor_1 (xor_1_out, MS1, MS2);
  xor xor_2 (xor_2_out, MS2, Res);
  not not_1 (not_1_out, xor_1_out);
  and and_1 (overflow, not_1_out, xor_2_out);
endmodule

module AND_4bit_a_bit (
  input  [3:0] A,
  input  [3:0] B,
  output [3:0] Res
);

  and and_1 (Res[0], A[0], B[0]);
  and and_2 (Res[1], A[1], B[1]);
  and and_3 (Res[2], A[2], B[2]);
  and and_4 (Res[3], B[3], A[3]);
endmodule

module OR_4bit_a_bit (
  input  [3:0] A,
  input  [3:0] B,
  output [3:0] Res
);

  or or_1 (Res[0], A[0], B[0]);
  or or_2 (Res[1], A[1], B[1]);
  or or_3 (Res[2], A[2], B[2]);
  or or_4 (Res[3], B[3], A[3]);
endmodule
